// Logisim project L01_task3.circ as structural Verilog: 1 circuit, main circuit main
module main (
  input  in_1,
  input  in_2,
  input  in_3,
  input  in_4,
  input  in_5,
  input  in_6,
  input  in_7,
  output NOT_GATE,
  output AND_GATE,
  output NAND_GATE,
  output OR_GATE,
  output NOR_GATE,
  output XOR_GATE,
  output XNOR_GATE
);

  not not_1 (NOT_GATE, in_1);
  and and_1 (AND_GATE, in_2, in_3);
  nand nand_1 (NAND_GATE, in_2, in_3);
  or or_1 (OR_GATE, in_4, in_5);
  nor nor_1 (NOR_GATE, in_4, in_5);
  xor xor_1 (XOR_GATE, in_6, in_7);
  xnor xnor_1 (XNOR_GATE, in_6, in_7);
endmodule
