// Logisim project lab01_task05.circ as structural Verilog: 1 circuit, main circuit main
module main (
  input  A,
  input  B,
  output C
);

  wire and_1_out, and_2_out, not_1_out, not_2_out;

  not not_1 (not_1_out, A);
  not not_2 (not_2_out, B);
  and and_1 (and_1_out, not_1_out, B);
  and and_2 (and_2_out, A, not_2_out);
  or or_1 (C, and_1_out, and_2_out);

  // Notes on the sheet:
  //   t1
  //   B
  //   A
  //   t2
  //   t3
  //   t4
endmodule
